// Logisim project 课程设计 .circ as structural Verilog: 18 circuits, main circuit 电梯状态转化模块
module \电梯  (
  input  in_1
);

  wire and_1_out, button_1_out, button_2_out, button_3_out, button_4_out, button_5_out, button_6_out,
       button_7_out, button_8_out, button_9_out, button_10_out, button_11_out, button_12_out, button_13_out,
       clock_1_out, door, not_1_out, \楼层_1_out_2 , \楼层_1_out_3 , \楼层_1_out_4 , \楼层_1_out_5 , \楼层_1_out_6 ;
  wire [1:0] up_down;
  wire [2:0] S;
  wire [4:0] in, inr;
  wire [6:0] \内部控制面板的上下楼_1_out_2 , \内部控制面板的上下楼_1_out_3 , \内部控制面板的上下楼_1_out_4 , \内部控制面板的上下楼_1_out_5 ,
       \内部控制面板的上下楼_1_out_6 ;
  wire [7:0] \梯外_1_out_10 ;
  wire [8:0] \梯外_1_out_11 , \梯外_1_out_12 , \梯外_1_out_13 , \梯外_1_out_14 , \梯外_1_out_15 , \梯外_1_out_16 ,
       \梯外_1_out_17 , \梯外_1_out_18 ;
  wire [9:0] \梯外控制面板_1_out_request , \梯外控制面板_1_out_request_2 ;

  Button button_1 (.out(button_1_out));
  Button button_2 (.out(button_2_out));
  Button button_3 (.out(button_3_out));
  Button button_4 (.out(button_4_out));
  Button button_5 (.out(button_5_out));
  Button button_6 (.out(button_6_out));
  Button button_7 (.out(button_7_out));
  Button button_8 (.out(button_8_out));
  Clock clock_1 (.out(clock_1_out));
  \梯外  \u_梯外_1  (
    .in_1(button_1_out), .in_3(button_2_out), .in_4(button_3_out), .in_5(button_4_out), .in_6(button_5_out),
    .in_7(button_6_out), .in_8(button_7_out), .in_9(button_8_out), .out_10(\梯外_1_out_10 ),
    .in_2(\梯外控制面板_1_out_request_2 ), .out_11(\梯外_1_out_11 ), .out_12(\梯外_1_out_12 ), .out_13(\梯外_1_out_13 ),
    .out_14(\梯外_1_out_14 ), .out_15(\梯外_1_out_15 ), .out_16(\梯外_1_out_16 ), .out_17(\梯外_1_out_17 ),
    .out_18(\梯外_1_out_18 ));
  \梯外控制面板  \u_梯外控制面板_1  (
    .clk(clock_1_out), .ReSet(in_1), .request(\梯外_1_out_10 ), .out_Request(\梯外控制面板_1_out_request ), .S(S),
    .up_down(up_down), .out_Request_2(\梯外控制面板_1_out_request_2 ));
  DotMatrix #(.matrixcols(3), .matrixrows(3)) dotmatrix_1 (
    .col0(\梯外_1_out_15 [8:6]), .col1(\梯外_1_out_15 [5:3]), .col2(\梯外_1_out_15 [2:0]));
  DotMatrix #(.matrixcols(3), .matrixrows(3)) dotmatrix_2 (
    .col0(\梯外_1_out_11 [8:6]), .col1(\梯外_1_out_11 [5:3]), .col2(\梯外_1_out_11 [2:0]));
  DotMatrix #(.matrixcols(3), .matrixrows(3)) dotmatrix_3 (
    .col0(\梯外_1_out_16 [8:6]), .col1(\梯外_1_out_16 [5:3]), .col2(\梯外_1_out_16 [2:0]));
  DotMatrix #(.matrixcols(3), .matrixrows(3)) dotmatrix_4 (
    .col0(\梯外_1_out_12 [8:6]), .col1(\梯外_1_out_12 [5:3]), .col2(\梯外_1_out_12 [2:0]));
  DotMatrix #(.matrixcols(3), .matrixrows(3)) dotmatrix_5 (
    .col0(\梯外_1_out_17 [8:6]), .col1(\梯外_1_out_17 [5:3]), .col2(\梯外_1_out_17 [2:0]));
  DotMatrix #(.matrixcols(3), .matrixrows(3)) dotmatrix_6 (
    .col0(\梯外_1_out_13 [8:6]), .col1(\梯外_1_out_13 [5:3]), .col2(\梯外_1_out_13 [2:0]));
  DotMatrix #(.matrixcols(3), .matrixrows(3)) dotmatrix_7 (
    .col0(\梯外_1_out_18 [8:6]), .col1(\梯外_1_out_18 [5:3]), .col2(\梯外_1_out_18 [2:0]));
  DotMatrix #(.matrixcols(3), .matrixrows(3)) dotmatrix_8 (
    .col0(\梯外_1_out_14 [8:6]), .col1(\梯外_1_out_14 [5:3]), .col2(\梯外_1_out_14 [2:0]));
  Hex_Digit_Display hex_digit_display_1 (.value({1'b0, S}));  // open: dp
  Button button_9 (.out(button_9_out));
  Button button_10 (.out(button_10_out));
  Button button_11 (.out(button_11_out));
  Button button_12 (.out(button_12_out));
  Button button_13 (.out(button_13_out));
  DotMatrix dotmatrix_9 (
    .col0(\内部控制面板的上下楼_1_out_2 ), .col1(\内部控制面板的上下楼_1_out_3 ), .col2(\内部控制面板的上下楼_1_out_4 ),
    .col3(\内部控制面板的上下楼_1_out_5 ), .col4(\内部控制面板的上下楼_1_out_6 ));
  \内部控制面板的上下楼  \u_内部控制面板的上下楼_1  (
    .up_down(up_down), .out_2(\内部控制面板的上下楼_1_out_2 ), .out_3(\内部控制面板的上下楼_1_out_3 ),
    .out_4(\内部控制面板的上下楼_1_out_4 ), .out_5(\内部控制面板的上下楼_1_out_5 ), .out_6(\内部控制面板的上下楼_1_out_6 ));
  LED led_1 (.in(door));
  \梯内  \u_梯内_1  (
    .in_1(button_9_out), .in_2(button_10_out), .in_3(button_11_out), .in_4(button_12_out),
    .in_5(button_13_out), .out_6(in));
  \楼层  \u_楼层_1  (
    .in_1(inr), .out_2(\楼层_1_out_2 ), .out_3(\楼层_1_out_3 ), .out_4(\楼层_1_out_4 ), .out_5(\楼层_1_out_5 ),
    .out_6(\楼层_1_out_6 ));
  LED led_2 (.in(\楼层_1_out_2 ));
  LED led_3 (.in(\楼层_1_out_3 ));
  LED led_4 (.in(\楼层_1_out_4 ));
  LED led_5 (.in(\楼层_1_out_5 ));
  LED led_6 (.in(\楼层_1_out_6 ));
  \电梯内部控制面板  \u_电梯内部控制面板_1  (
    .clk(clock_1_out), .ReSet(in_1), .request(in), .S(S), .out_request(\梯外控制面板_1_out_request ),
    .in_Request(inr), .door(door));
  and and_1 (and_1_out, clock_1_out, not_1_out);
  not not_1 (not_1_out, door);
  \电梯状态转化模块  \u_电梯状态转化模块_1  (.clk(and_1_out), .ReSet(in_1), .up_down(up_down), .S_next(S));
  \电梯升降模式转换模块  \u_电梯升降模式转换模块_1  (
    .clk(and_1_out), .ReSet(in_1), .S(S), .in_request(inr), .out_request(\梯外控制面板_1_out_request ),
    .up_down(up_down));
endmodule

module \电梯状态转化模块  (
  input  clk,
  input  ReSet,
  input  [1:0] up_down,
  output [2:0] S_next
);

  wire and_1_out, and_2_out, and_3_out, and_4_out, and_5_out, and_6_out, and_7_out, and_8_out, and_9_out,
       and_10_out, and_11_out, and_12_out, and_13_out, and_14_out, and_15_out, and_16_out, not_1_out,
       not_2_out, not_3_out, not_4_out, not_5_out, not_6_out, not_7_out, not_8_out, not_9_out, not_10_out,
       not_11_out, not_12_out, not_13_out, not_14_out, not_15_out, not_16_out, not_17_out, not_18_out,
       not_19_out, not_20_out, not_21_out, not_22_out, not_23_out, not_24_out, not_25_out, not_26_out,
       not_27_out, not_28_out, not_29_out, or_1_out, or_2_out, or_3_out;

  not not_1 (not_1_out, ReSet);
  not not_2 (not_2_out, up_down[1]);
  not not_3 (not_3_out, ReSet);
  not not_4 (not_4_out, up_down[0]);
  not not_5 (not_5_out, ReSet);
  not not_6 (not_6_out, ReSet);
  not not_7 (not_7_out, ReSet);
  not not_8 (not_8_out, up_down[1]);
  not not_9 (not_9_out, ReSet);
  not not_10 (not_10_out, up_down[1]);
  not not_11 (not_11_out, S_next[2]);
  not not_12 (not_12_out, S_next[0]);
  not not_13 (not_13_out, ReSet);
  not not_14 (not_14_out, up_down[0]);
  not not_15 (not_15_out, ReSet);
  not not_16 (not_16_out, up_down[1]);
  not not_17 (not_17_out, S_next[2]);
  not not_18 (not_18_out, S_next[1]);
  not not_19 (not_19_out, ReSet);
  not not_20 (not_20_out, ReSet);
  not not_21 (not_21_out, S_next[0]);
  not not_22 (not_22_out, up_down[0]);
  not not_23 (not_23_out, S_next[2]);
  not not_24 (not_24_out, S_next[0]);
  not not_25 (not_25_out, up_down[1]);
  not not_26 (not_26_out, S_next[1]);
  not not_27 (not_27_out, S_next[0]);
  not not_28 (not_28_out, S_next[2]);
  not not_29 (not_29_out, S_next[1]);
  and and_1 (and_1_out, not_1_out, not_2_out, S_next[2]);
  and and_2 (and_2_out, not_3_out, not_4_out, S_next[2]);
  and and_3 (and_3_out, not_5_out, S_next[2], S_next[0]);
  and and_4 (and_4_out, not_6_out, S_next[2], S_next[1]);
  and and_5 (and_5_out, not_7_out, not_8_out, up_down[0], S_next[1], S_next[0]);
  and and_6 (and_6_out, not_9_out, not_10_out, not_11_out, S_next[1], not_12_out);
  and and_7 (and_7_out, not_13_out, not_14_out, S_next[1]);
  and and_8 (and_8_out, not_15_out, not_16_out, up_down[0], not_17_out, not_18_out, S_next[0]);
  and and_9 (and_9_out, not_19_out, up_down[1], S_next[1], S_next[0]);
  and and_10 (and_10_out, not_20_out, up_down[1], up_down[0], S_next[2], not_21_out);
  and and_11 (and_11_out, not_22_out, S_next[0]);
  and and_12 (and_12_out, S_next[2], S_next[1], S_next[0]);
  and and_13 (and_13_out, up_down[0], not_23_out, S_next[1], not_24_out);
  and and_14 (and_14_out, not_25_out, up_down[0], S_next[2]);
  and and_15 (and_15_out, up_down[0], S_next[2], not_26_out, not_27_out);
  and and_16 (and_16_out, up_down[1], not_28_out, not_29_out, S_next[0]);
  or or_1 (or_1_out, and_1_out, and_2_out, and_3_out, and_4_out, and_5_out);
  or or_2 (or_2_out, and_6_out, and_7_out, and_8_out, and_9_out, and_10_out);
  or or_3 (or_3_out, and_11_out, and_12_out, and_13_out, and_14_out, and_15_out, and_16_out, ReSet);
  D_Flip_Flop d_ff_1 (.clk(clk), .D(or_1_out), .Q(S_next[2]));  // open: Qn, preset, en, reset
  D_Flip_Flop d_ff_2 (.clk(clk), .D(or_2_out), .Q(S_next[1]));  // open: Qn, preset, en, reset
  D_Flip_Flop d_ff_3 (.clk(clk), .D(or_3_out), .Q(S_next[0]));  // open: Qn, preset, en, reset

  // Other names for the same wires on the sheet: S1_next = S_next[0]; S2_next = S_next[1]; S3_next = S_next[2]
endmodule

module \电梯升降模式转换模块  (
  input  clk,
  input  ReSet,
  input  [2:0] S,
  input  [4:0] in_request,
  input  [9:0] out_request,
  output [1:0] up_down
);

  wire _00_0, _00_1, _01_0, _01_1, _11_0, _11_1, multiplexer_1_out, multiplexer_2_out, not_1_out, not_2_out;
  wire [1:0] up_down_t;

  _00 u_00_1 (.S(S), .in_request(in_request), .out_request(out_request), ._00_1(_00_1), ._00_0(_00_0));
  _01 u_01_1 (.S(S), .in_request(in_request), .out_request(out_request), ._00_1(_01_1), ._00_0(_01_0));
  _11 u_11_1 (.S(S), .in_request(in_request), .out_request(out_request), ._00_1(_11_1), ._00_0(_11_0));
  Multiplexer #(.select(2), .enable("false")) multiplexer_1 (
    .in0(_00_1), .in1(_01_1), .in3(_11_1), .out(multiplexer_1_out), .sel(up_down_t));  // open: in2
  Multiplexer #(.select(2), .enable("false")) multiplexer_2 (
    .in0(_00_0), .in1(_01_0), .in3(_11_0), .out(multiplexer_2_out), .sel(up_down_t));  // open: in2
  not not_1 (not_1_out, ReSet);
  not not_2 (not_2_out, ReSet);
  and and_1 (up_down[1], not_1_out, multiplexer_1_out);
  and and_2 (up_down[0], not_2_out, multiplexer_2_out);
  D_Flip_Flop d_ff_1 (.clk(clk), .D(up_down[1]), .Q(up_down_t[1]));  // open: Qn, preset, en, reset
  D_Flip_Flop d_ff_2 (.clk(clk), .D(up_down[0]), .Q(up_down_t[0]));  // open: Qn, preset, en, reset
endmodule

module \电梯开门模块  (
  input  clk,
  input  [2:0] S,
  input  [4:0] in_request,
  input  [9:0] out_request,
  output out_5
);

  wire and_1_out, and_2_out, and_3_out, and_4_out, and_5_out, and_6_out, and_7_out, and_8_out, and_9_out,
       and_10_out, d_ff_1_q, d_ff_2_q, not_1_out, or_1_out, or_2_out, or_3_out, or_4_out, or_5_out, or_6_out,
       or_7_out, or_8_out, \判断层数_1_f1 , \判断层数_1_f2 , \判断层数_1_f3 , \判断层数_1_f4 , \判断层数_1_f5 ;

  \判断层数  \u_判断层数_1  (.S(S), .f5(\判断层数_1_f5 ), .f4(\判断层数_1_f4 ), .f3(\判断层数_1_f3 ), .f2(\判断层数_1_f2 ), .f1(\判断层数_1_f1 ));
  or or_1 (or_1_out, out_request[0], out_request[1]);
  or or_2 (or_2_out, out_request[2], out_request[3]);
  or or_3 (or_3_out, out_request[4], out_request[5]);
  and and_1 (and_1_out, \判断层数_1_f5 , in_request[4]);
  and and_2 (and_2_out, \判断层数_1_f4 , in_request[3]);
  and and_3 (and_3_out, \判断层数_1_f3 , in_request[2]);
  and and_4 (and_4_out, \判断层数_1_f2 , in_request[1]);
  and and_5 (and_5_out, \判断层数_1_f1 , in_request[0]);
  or or_4 (or_4_out, out_request[6], out_request[7]);
  or or_5 (or_5_out, out_request[8], out_request[9]);
  or or_6 (or_6_out, and_1_out, and_2_out, and_3_out, and_4_out, and_5_out);
  and and_6 (and_6_out, \判断层数_1_f5 , or_5_out);
  and and_7 (and_7_out, \判断层数_1_f4 , or_4_out);
  and and_8 (and_8_out, \判断层数_1_f3 , or_3_out);
  and and_9 (and_9_out, \判断层数_1_f2 , or_2_out);
  and and_10 (and_10_out, \判断层数_1_f1 , or_1_out);
  or or_7 (or_7_out, and_6_out, and_7_out, and_8_out, and_9_out, and_10_out);
  or or_8 (or_8_out, or_6_out, or_7_out);
  and and_11 (out_5, or_8_out, not_1_out);
  not not_1 (not_1_out, d_ff_2_q);
  D_Flip_Flop d_ff_1 (.clk(clk), .D(out_5), .Q(d_ff_1_q));  // open: Qn, preset, en, reset
  D_Flip_Flop d_ff_2 (.clk(clk), .D(d_ff_1_q), .Q(d_ff_2_q));  // open: Qn, preset, en, reset
endmodule

module \梯外控制面板  (
  input  clk,
  input  ReSet,
  input  [7:0] request,
  input  [1:0] up_down,
  input  [2:0] S,
  output [9:0] out_Request,
  output [9:0] out_Request_2
);

  wire and_1_out, and_2_out, and_3_out, and_4_out, and_5_out, and_6_out, and_7_out, and_8_out, and_9_out,
       and_10_out, and_11_out, and_12_out, d_ff_1_qn, d_ff_2_qn, d_ff_3_qn, d_ff_4_qn, d_ff_5_qn, d_ff_6_qn,
       d_ff_7_qn, d_ff_8_qn, f1_up, f2_down, f2_up, f3_down, f3_up, f4_down, f4_up, f5_down,
       multiplexer_1_out, multiplexer_2_out, multiplexer_3_out, multiplexer_4_out, multiplexer_5_out,
       multiplexer_6_out, multiplexer_7_out, multiplexer_8_out, multiplexer_9_out, multiplexer_10_out,
       multiplexer_11_out, multiplexer_12_out, multiplexer_13_out, multiplexer_14_out, multiplexer_15_out,
       multiplexer_16_out, not_1_out, not_2_out, not_3_out, not_4_out, not_5_out, not_6_out, not_7_out,
       not_8_out, not_9_out, not_10_out, not_11_out;

  not not_1 (not_1_out, up_down[1]);
  and and_1 (and_1_out, not_1_out, up_down[0]);
  and and_2 (and_2_out, up_down[1], up_down[0]);
  Multiplexer #(.enable("false")) multiplexer_1 (
    .in0(1'b1), .in1(request[6]), .out(multiplexer_1_out), .sel(d_ff_2_qn));
  Multiplexer #(.enable("false")) multiplexer_2 (
    .in0(1'b1), .in1(request[5]), .out(multiplexer_2_out), .sel(d_ff_3_qn));
  Multiplexer #(.enable("false")) multiplexer_3 (
    .in0(1'b1), .in1(request[1]), .out(multiplexer_3_out), .sel(d_ff_7_qn));
  Multiplexer #(.enable("false")) multiplexer_4 (
    .in0(1'b1), .in1(request[0]), .out(multiplexer_4_out), .sel(d_ff_8_qn));
  Multiplexer #(.enable("false")) multiplexer_5 (
    .in0(1'b1), .in1(request[7]), .out(multiplexer_5_out), .sel(d_ff_1_qn));
  Multiplexer #(.enable("false")) multiplexer_6 (
    .in0(1'b1), .in1(request[4]), .out(multiplexer_6_out), .sel(d_ff_4_qn));
  Multiplexer #(.enable("false")) multiplexer_7 (
    .in0(1'b1), .in1(request[3]), .out(multiplexer_7_out), .sel(d_ff_5_qn));
  Multiplexer #(.enable("false")) multiplexer_8 (
    .in0(1'b1), .in1(request[2]), .out(multiplexer_8_out), .sel(d_ff_6_qn));
  \out_判断层数  \out_判断层数_1  (
    .S(S), .up(and_1_out), .down(and_2_out), .f5_down(f5_down), .f4_up(f4_up), .f4_down(f4_down),
    .f3_up(f3_up), .f3_down(f3_down), .f2_up(f2_up), .f2_down(f2_down), .f1_up(f1_up));
  Multiplexer #(.enable("false")) multiplexer_9 (
    .in0(multiplexer_5_out), .in1(1'b0), .out(multiplexer_9_out), .sel(f5_down));
  Multiplexer #(.enable("false")) multiplexer_10 (
    .in0(multiplexer_1_out), .in1(1'b0), .out(multiplexer_10_out), .sel(f4_up));
  Multiplexer #(.enable("false")) multiplexer_11 (
    .in0(multiplexer_2_out), .in1(1'b0), .out(multiplexer_11_out), .sel(f4_down));
  Multiplexer #(.enable("false")) multiplexer_12 (
    .in0(multiplexer_6_out), .in1(1'b0), .out(multiplexer_12_out), .sel(f3_up));
  Multiplexer #(.enable("false")) multiplexer_13 (
    .in0(multiplexer_7_out), .in1(1'b0), .out(multiplexer_13_out), .sel(f3_down));
  Multiplexer #(.enable("false")) multiplexer_14 (
    .in0(multiplexer_8_out), .in1(1'b0), .out(multiplexer_14_out), .sel(f2_up));
  Multiplexer #(.enable("false")) multiplexer_15 (
    .in0(multiplexer_3_out), .in1(1'b0), .out(multiplexer_15_out), .sel(f2_down));
  Multiplexer #(.enable("false")) multiplexer_16 (
    .in0(multiplexer_4_out), .in1(1'b0), .out(multiplexer_16_out), .sel(f1_up));
  not not_2 (not_2_out, ReSet);
  and and_3 (and_3_out, not_2_out, multiplexer_9_out);
  not not_3 (not_3_out, ReSet);
  and and_4 (and_4_out, not_3_out, multiplexer_10_out);
  not not_4 (not_4_out, ReSet);
  and and_5 (and_5_out, not_4_out, multiplexer_11_out);
  not not_5 (not_5_out, ReSet);
  and and_6 (and_6_out, not_5_out, multiplexer_12_out);
  not not_6 (not_6_out, ReSet);
  and and_7 (and_7_out, not_6_out, multiplexer_13_out);
  not not_7 (not_7_out, ReSet);
  and and_8 (and_8_out, not_7_out, multiplexer_14_out);
  not not_8 (not_8_out, ReSet);
  and and_9 (and_9_out, not_8_out, multiplexer_15_out);
  not not_9 (not_9_out, ReSet);
  and and_10 (and_10_out, not_9_out, multiplexer_16_out);
  not not_10 (not_10_out, ReSet);
  and and_11 (and_11_out, not_10_out, 1'b0);
  not not_11 (not_11_out, ReSet);
  and and_12 (and_12_out, not_11_out, 1'b0);
  D_Flip_Flop d_ff_1 (.clk(clk), .D(and_3_out), .Q(out_Request[8]), .Qn(d_ff_1_qn));  // open: preset, en, reset
  D_Flip_Flop d_ff_2 (.clk(clk), .D(and_4_out), .Q(out_Request[7]), .Qn(d_ff_2_qn));  // open: preset, en, reset
  D_Flip_Flop d_ff_3 (.clk(clk), .D(and_5_out), .Q(out_Request[6]), .Qn(d_ff_3_qn));  // open: preset, en, reset
  D_Flip_Flop d_ff_4 (.clk(clk), .D(and_6_out), .Q(out_Request[5]), .Qn(d_ff_4_qn));  // open: preset, en, reset
  D_Flip_Flop d_ff_5 (.clk(clk), .D(and_7_out), .Q(out_Request[4]), .Qn(d_ff_5_qn));  // open: preset, en, reset
  D_Flip_Flop d_ff_6 (.clk(clk), .D(and_8_out), .Q(out_Request[3]), .Qn(d_ff_6_qn));  // open: preset, en, reset
  D_Flip_Flop d_ff_7 (.clk(clk), .D(and_9_out), .Q(out_Request[2]), .Qn(d_ff_7_qn));  // open: preset, en, reset
  D_Flip_Flop d_ff_8 (.clk(clk), .D(and_10_out), .Q(out_Request[1]), .Qn(d_ff_8_qn));  // open: preset, en, reset
  D_Flip_Flop d_ff_9 (.clk(clk), .D(and_11_out), .Q(out_Request[9]));  // open: Qn, preset, en, reset
  D_Flip_Flop d_ff_10 (.clk(clk), .D(and_12_out), .Q(out_Request[0]));  // open: Qn, preset, en, reset

  assign out_Request_2 = out_Request;
endmodule

module \out_判断层数  (
  input  [2:0] S,
  input  up,
  input  down,
  output f5_down,
  output f4_up,
  output f4_down,
  output f3_up,
  output f3_down,
  output f2_up,
  output f2_down,
  output f1_up
);

  wire not_1_out, not_2_out, not_3_out, not_4_out, not_5_out, not_6_out, not_7_out, not_8_out, not_9_out,
       not_10_out, not_11_out, not_12_out, not_13_out, not_14_out, not_15_out, not_16_out, not_17_out,
       not_18_out, not_19_out, not_20_out, not_21_out;

  not not_1 (not_1_out, S[1]);
  not not_2 (not_2_out, up);
  not not_3 (not_3_out, S[1]);
  not not_4 (not_4_out, S[0]);
  not not_5 (not_5_out, down);
  not not_6 (not_6_out, S[1]);
  not not_7 (not_7_out, S[0]);
  not not_8 (not_8_out, up);
  not not_9 (not_9_out, S[2]);
  not not_10 (not_10_out, down);
  not not_11 (not_11_out, S[2]);
  not not_12 (not_12_out, up);
  not not_13 (not_13_out, S[2]);
  not not_14 (not_14_out, S[0]);
  not not_15 (not_15_out, down);
  not not_16 (not_16_out, S[2]);
  not not_17 (not_17_out, S[0]);
  not not_18 (not_18_out, up);
  not not_19 (not_19_out, S[2]);
  not not_20 (not_20_out, S[1]);
  not not_21 (not_21_out, down);
  and and_1 (f5_down, S[2], not_1_out, S[0], down, not_2_out);
  and and_2 (f4_up, S[2], not_3_out, not_4_out, up, not_5_out);
  and and_3 (f4_down, S[2], not_6_out, not_7_out, not_8_out, down);
  and and_4 (f3_up, not_9_out, S[1], S[0], up, not_10_out);
  and and_5 (f3_down, not_11_out, S[1], S[0], not_12_out, down);
  and and_6 (f2_up, not_13_out, S[1], not_14_out, up, not_15_out);
  and and_7 (f2_down, not_16_out, S[1], not_17_out, not_18_out, down);
  and and_8 (f1_up, not_19_out, not_20_out, S[0], up, not_21_out);
endmodule

module \电梯内部控制面板  (
  input  clk,
  input  ReSet,
  input  [4:0] request,
  input  [2:0] S,
  input  [9:0] out_request,
  output [4:0] in_Request,
  output door
);

  wire and_1_out, and_2_out, and_3_out, and_4_out, and_5_out, d_ff_1_qn, d_ff_2_qn, d_ff_3_qn, d_ff_4_qn,
       d_ff_5_qn, f1, f2, f3, f4, f5, multiplexer_1_out, multiplexer_2_out, multiplexer_3_out,
       multiplexer_4_out, multiplexer_5_out, multiplexer_6_out, multiplexer_7_out, multiplexer_8_out,
       multiplexer_9_out, multiplexer_10_out, not_1_out, not_2_out, not_3_out, not_4_out, not_5_out;

  \判断层数  \u_判断层数_1  (.S(S), .f5(f5), .f4(f4), .f3(f3), .f2(f2), .f1(f1));
  Multiplexer #(.enable("false")) multiplexer_1 (
    .in0(1'b1), .in1(request[4]), .out(multiplexer_1_out), .sel(d_ff_1_qn));
  Multiplexer #(.enable("false")) multiplexer_2 (
    .in0(1'b1), .in1(request[3]), .out(multiplexer_2_out), .sel(d_ff_2_qn));
  Multiplexer #(.enable("false")) multiplexer_3 (
    .in0(1'b1), .in1(request[2]), .out(multiplexer_3_out), .sel(d_ff_3_qn));
  Multiplexer #(.enable("false")) multiplexer_4 (
    .in0(1'b1), .in1(request[1]), .out(multiplexer_4_out), .sel(d_ff_4_qn));
  Multiplexer #(.enable("false")) multiplexer_5 (
    .in0(1'b1), .in1(request[0]), .out(multiplexer_5_out), .sel(d_ff_5_qn));
  Multiplexer #(.enable("false")) multiplexer_6 (
    .in0(multiplexer_1_out), .in1(1'b0), .out(multiplexer_6_out), .sel(f5));
  Multiplexer #(.enable("false")) multiplexer_7 (
    .in0(multiplexer_2_out), .in1(1'b0), .out(multiplexer_7_out), .sel(f4));
  Multiplexer #(.enable("false")) multiplexer_8 (
    .in0(multiplexer_3_out), .in1(1'b0), .out(multiplexer_8_out), .sel(f3));
  Multiplexer #(.enable("false")) multiplexer_9 (
    .in0(multiplexer_4_out), .in1(1'b0), .out(multiplexer_9_out), .sel(f2));
  Multiplexer #(.enable("false")) multiplexer_10 (
    .in0(multiplexer_5_out), .in1(1'b0), .out(multiplexer_10_out), .sel(f1));
  not not_1 (not_1_out, ReSet);
  not not_2 (not_2_out, ReSet);
  not not_3 (not_3_out, ReSet);
  not not_4 (not_4_out, ReSet);
  not not_5 (not_5_out, ReSet);
  and and_1 (and_1_out, not_1_out, multiplexer_6_out);
  and and_2 (and_2_out, not_2_out, multiplexer_7_out);
  and and_3 (and_3_out, not_3_out, multiplexer_8_out);
  and and_4 (and_4_out, not_4_out, multiplexer_9_out);
  and and_5 (and_5_out, not_5_out, multiplexer_10_out);
  D_Flip_Flop d_ff_1 (.clk(clk), .D(and_1_out), .Q(in_Request[4]), .Qn(d_ff_1_qn));  // open: preset, en, reset
  D_Flip_Flop d_ff_2 (.clk(clk), .D(and_2_out), .Q(in_Request[3]), .Qn(d_ff_2_qn));  // open: preset, en, reset
  D_Flip_Flop d_ff_3 (.clk(clk), .D(and_3_out), .Q(in_Request[2]), .Qn(d_ff_3_qn));  // open: preset, en, reset
  D_Flip_Flop d_ff_4 (.clk(clk), .D(and_4_out), .Q(in_Request[1]), .Qn(d_ff_4_qn));  // open: preset, en, reset
  D_Flip_Flop d_ff_5 (.clk(clk), .D(and_5_out), .Q(in_Request[0]), .Qn(d_ff_5_qn));  // open: preset, en, reset
  \电梯开门模块  \u_电梯开门模块_1  (.clk(clk), .S(S), .in_request(in_Request), .out_request(out_request), .out_5(door));
endmodule

module \判断层数  (
  input  [2:0] S,
  output f5,
  output f4,
  output f3,
  output f2,
  output f1
);

  wire not_1_out, not_2_out, not_3_out, not_4_out, not_5_out, not_6_out, not_7_out, not_8_out;

  not not_1 (not_1_out, S[1]);
  not not_2 (not_2_out, S[1]);
  not not_3 (not_3_out, S[0]);
  not not_4 (not_4_out, S[2]);
  not not_5 (not_5_out, S[2]);
  not not_6 (not_6_out, S[0]);
  not not_7 (not_7_out, S[2]);
  not not_8 (not_8_out, S[1]);
  and and_1 (f5, S[2], not_1_out, S[0]);
  and and_2 (f4, S[2], not_2_out, not_3_out);
  and and_3 (f3, not_4_out, S[1], S[0]);
  and and_4 (f2, not_5_out, S[1], not_6_out);
  and and_5 (f1, not_7_out, not_8_out, S[0]);
endmodule

module _00 (
  input  [2:0] S,
  input  [4:0] in_request,
  input  [9:0] out_request,
  output _00_0,
  output _00_1
);

  wire comparator_1_gt, comparator_2_gt, comparator_3_gt, comparator_4_gt, comparator_5_gt, comparator_6_gt;
  wire [2:0] subtractor_1_out, subtractor_2_out, subtractor_3_out, subtractor_4_out, subtractor_5_out;
  wire [4:0] shifter_1_out, shifter_2_out, shifter_3_out, shifter_4_out, shifter_5_out, shifter_6_out,
       shifter_7_out, shifter_8_out;

  Subtractor #(.width(3)) subtractor_1 (.a(3'b110), .b(S), .out(subtractor_1_out));  // open: bin, bout
  Subtractor #(.width(3)) subtractor_2 (.a(S), .b(3'b001), .out(subtractor_2_out));  // open: bin, bout
  Subtractor #(.width(3)) subtractor_3 (.a(S), .b(3'b001), .out(subtractor_3_out));  // open: bin, bout
  Subtractor #(.width(3)) subtractor_4 (.a(3'b110), .b(S), .out(subtractor_4_out));  // open: bin, bout
  Subtractor #(.width(3)) subtractor_5 (.a(3'b110), .b(S), .out(subtractor_5_out));  // open: bin, bout
  Shifter #(.width(5)) shifter_1 (.in(in_request), .\dist (subtractor_1_out), .out(shifter_1_out));
  Shifter #(.width(5), .shift("lr")) shifter_2 (.in(in_request), .\dist (S), .out(shifter_2_out));
  Shifter #(.width(5), .shift("lr")) shifter_3 (
    .in({out_request[8], out_request[6], out_request[4], out_request[2], out_request[0]}), .\dist (S),
    .out(shifter_3_out));
  Shifter #(.width(5), .shift("lr")) shifter_4 (
    .in({out_request[9], out_request[7], out_request[5], out_request[3], out_request[1]}), .\dist (S),
    .out(shifter_4_out));
  Shifter #(.width(5)) shifter_5 (
    .in({out_request[8], out_request[6], out_request[4], out_request[2], out_request[0]}),
    .\dist (subtractor_2_out), .out(shifter_5_out));
  Shifter #(.width(5)) shifter_6 (
    .in({out_request[9], out_request[7], out_request[5], out_request[3], out_request[1]}),
    .\dist (subtractor_3_out), .out(shifter_6_out));
  Shifter #(.width(5)) shifter_7 (
    .in({out_request[8], out_request[6], out_request[4], out_request[2], out_request[0]}),
    .\dist (subtractor_4_out), .out(shifter_7_out));
  Shifter #(.width(5)) shifter_8 (
    .in({out_request[9], out_request[7], out_request[5], out_request[3], out_request[1]}),
    .\dist (subtractor_5_out), .out(shifter_8_out));
  Comparator #(.width(5), .mode("unsigned")) comparator_1 (
    .a(shifter_1_out), .b({5{1'b0}}), .gt(comparator_1_gt));  // open: eq, lt
  Comparator #(.width(5)) comparator_2 (.a(shifter_2_out), .b({5{1'b0}}), .gt(comparator_2_gt));  // open: eq, lt
  Comparator #(.width(5), .mode("unsigned")) comparator_3 (
    .a(shifter_3_out), .b({5{1'b0}}), .gt(comparator_3_gt));  // open: eq, lt
  Comparator #(.width(5), .mode("unsigned")) comparator_4 (
    .a(shifter_4_out), .b({5{1'b0}}), .gt(comparator_4_gt));  // open: eq, lt
  Comparator #(.width(5), .mode("unsigned")) comparator_5 (
    .a(shifter_7_out), .b({5{1'b0}}), .gt(comparator_5_gt));  // open: eq, lt
  Comparator #(.width(5), .mode("unsigned")) comparator_6 (
    .a(shifter_8_out), .b({5{1'b0}}), .gt(comparator_6_gt));  // open: eq, lt
  \_00状态  \u_00状态_1  (
    .in_down(comparator_1_gt), .in_up(comparator_2_gt), .out_up_down(comparator_3_gt),
    .out_up_up(comparator_4_gt), .out_down_down(comparator_5_gt), .out_down_up(comparator_6_gt),
    .next_0(_00_0), .next_1(_00_1));

  // Other names for the same wires on the sheet: out_request_down[4:0] = {out_request[8], out_request[6], out_request[4], out_request[2], out_request[0]};
  //   out_request_up[4:0] = {out_request[9], out_request[7], out_request[5], out_request[3], out_request[1]}

  // Notes on the sheet:
  //   表示楼下有in_quest
  //   表示楼上有in_quest
  //   表示楼上有out_quest_down
  //   表示楼上有out_quest_up
  //   表示楼下有out_quest_down
  //   表示楼下有out_quest_up
endmodule

module \_00状态  (
  input  in_down,
  input  in_up,
  input  out_up_down,
  input  out_up_up,
  input  out_down_down,
  input  out_down_up,
  output next_0,
  output next_1
);

  wire not_1_out, not_2_out, or_2_out;

  or or_1 (next_0, in_up, in_down, out_up_down, out_up_up, out_down_up, out_down_down);
  or or_2 (or_2_out, in_down, out_down_up, out_down_down);
  not not_1 (not_1_out, in_up);
  not not_2 (not_2_out, out_up_down);
  and and_1 (next_1, or_2_out, not_1_out, not_2_out);
endmodule

module _01 (
  input  [2:0] S,
  input  [4:0] in_request,
  input  [9:0] out_request,
  output _00_0,
  output _00_1
);

  wire comparator_1_gt, comparator_2_gt, comparator_3_gt, comparator_4_gt, comparator_5_gt, comparator_6_gt;
  wire [2:0] subtractor_1_out, subtractor_2_out, subtractor_3_out, subtractor_4_out, subtractor_5_out;
  wire [4:0] shifter_1_out, shifter_2_out, shifter_3_out, shifter_4_out, shifter_5_out, shifter_6_out,
       shifter_7_out, shifter_8_out;

  Subtractor #(.width(3)) subtractor_1 (.a(3'b110), .b(S), .out(subtractor_1_out));  // open: bin, bout
  Subtractor #(.width(3)) subtractor_2 (.a(S), .b(3'b001), .out(subtractor_2_out));  // open: bin, bout
  Subtractor #(.width(3)) subtractor_3 (.a(S), .b(3'b001), .out(subtractor_3_out));  // open: bin, bout
  Subtractor #(.width(3)) subtractor_4 (.a(3'b110), .b(S), .out(subtractor_4_out));  // open: bin, bout
  Subtractor #(.width(3)) subtractor_5 (.a(3'b110), .b(S), .out(subtractor_5_out));  // open: bin, bout
  Shifter #(.width(5)) shifter_1 (.in(in_request), .\dist (subtractor_1_out), .out(shifter_1_out));
  Shifter #(.width(5), .shift("lr")) shifter_2 (.in(in_request), .\dist (S), .out(shifter_2_out));
  Shifter #(.width(5), .shift("lr")) shifter_3 (
    .in({out_request[8], out_request[6], out_request[4], out_request[2], out_request[0]}), .\dist (S),
    .out(shifter_3_out));
  Shifter #(.width(5), .shift("lr")) shifter_4 (
    .in({out_request[9], out_request[7], out_request[5], out_request[3], out_request[1]}), .\dist (S),
    .out(shifter_4_out));
  Shifter #(.width(5)) shifter_5 (
    .in({out_request[8], out_request[6], out_request[4], out_request[2], out_request[0]}),
    .\dist (subtractor_2_out), .out(shifter_5_out));
  Shifter #(.width(5)) shifter_6 (
    .in({out_request[9], out_request[7], out_request[5], out_request[3], out_request[1]}),
    .\dist (subtractor_3_out), .out(shifter_6_out));
  Shifter #(.width(5)) shifter_7 (
    .in({out_request[8], out_request[6], out_request[4], out_request[2], out_request[0]}),
    .\dist (subtractor_4_out), .out(shifter_7_out));
  Shifter #(.width(5)) shifter_8 (
    .in({out_request[9], out_request[7], out_request[5], out_request[3], out_request[1]}),
    .\dist (subtractor_5_out), .out(shifter_8_out));
  Comparator #(.width(5), .mode("unsigned")) comparator_1 (
    .a(shifter_1_out), .b({5{1'b0}}), .gt(comparator_1_gt));  // open: eq, lt
  Comparator #(.width(5)) comparator_2 (.a(shifter_2_out), .b({5{1'b0}}), .gt(comparator_2_gt));  // open: eq, lt
  Comparator #(.width(5), .mode("unsigned")) comparator_3 (
    .a(shifter_3_out), .b({5{1'b0}}), .gt(comparator_3_gt));  // open: eq, lt
  Comparator #(.width(5), .mode("unsigned")) comparator_4 (
    .a(shifter_4_out), .b({5{1'b0}}), .gt(comparator_4_gt));  // open: eq, lt
  Comparator #(.width(5), .mode("unsigned")) comparator_5 (
    .a(shifter_7_out), .b({5{1'b0}}), .gt(comparator_5_gt));  // open: eq, lt
  Comparator #(.width(5), .mode("unsigned")) comparator_6 (
    .a(shifter_8_out), .b({5{1'b0}}), .gt(comparator_6_gt));  // open: eq, lt
  \_01状态  \u_01状态_1  (
    .in_up(comparator_2_gt), .in_down(comparator_1_gt), .out_up_down(comparator_3_gt),
    .out_up_up(comparator_4_gt), .out_down_down(comparator_5_gt), .out_down_up(comparator_6_gt),
    .next_0(_00_0), .next_1(_00_1));

  // Other names for the same wires on the sheet: out_request_down[4:0] = {out_request[8], out_request[6], out_request[4], out_request[2], out_request[0]};
  //   out_request_up[4:0] = {out_request[9], out_request[7], out_request[5], out_request[3], out_request[1]}

  // Notes on the sheet:
  //   表示楼下有in_quest
  //   表示楼上有in_quest
  //   表示楼上有out_quest_down
  //   表示楼上有out_quest_up
  //   表示楼下有out_quest_down
  //   表示楼下有out_quest_up
endmodule

module \_01状态  (
  input  in_up,
  input  in_down,
  input  out_up_down,
  input  out_up_up,
  input  out_down_down,
  input  out_down_up,
  output next_0,
  output next_1
);

  wire not_1_out, not_2_out, not_3_out, or_2_out;

  or or_1 (next_0, in_up, in_down, out_up_down, out_up_up, out_down_up, out_down_down);
  or or_2 (or_2_out, in_down, out_down_up, out_down_down);
  not not_1 (not_1_out, in_up);
  not not_2 (not_2_out, out_up_down);
  not not_3 (not_3_out, out_up_up);
  and and_1 (next_1, or_2_out, not_1_out, not_2_out, not_3_out);
endmodule

module _11 (
  input  [2:0] S,
  input  [4:0] in_request,
  input  [9:0] out_request,
  output _00_0,
  output _00_1
);

  wire comparator_1_gt, comparator_2_gt, comparator_3_gt, comparator_4_gt, comparator_5_gt, comparator_6_gt;
  wire [2:0] subtractor_1_out, subtractor_2_out, subtractor_3_out, subtractor_4_out, subtractor_5_out;
  wire [4:0] shifter_1_out, shifter_2_out, shifter_3_out, shifter_4_out, shifter_5_out, shifter_6_out,
       shifter_7_out, shifter_8_out;

  Subtractor #(.width(3)) subtractor_1 (.a(3'b110), .b(S), .out(subtractor_1_out));  // open: bin, bout
  Subtractor #(.width(3)) subtractor_2 (.a(S), .b(3'b001), .out(subtractor_2_out));  // open: bin, bout
  Subtractor #(.width(3)) subtractor_3 (.a(S), .b(3'b001), .out(subtractor_3_out));  // open: bin, bout
  Subtractor #(.width(3)) subtractor_4 (.a(3'b110), .b(S), .out(subtractor_4_out));  // open: bin, bout
  Subtractor #(.width(3)) subtractor_5 (.a(3'b110), .b(S), .out(subtractor_5_out));  // open: bin, bout
  Shifter #(.width(5)) shifter_1 (.in(in_request), .\dist (subtractor_1_out), .out(shifter_1_out));
  Shifter #(.width(5), .shift("lr")) shifter_2 (.in(in_request), .\dist (S), .out(shifter_2_out));
  Shifter #(.width(5), .shift("lr")) shifter_3 (
    .in({out_request[8], out_request[6], out_request[4], out_request[2], out_request[0]}), .\dist (S),
    .out(shifter_3_out));
  Shifter #(.width(5), .shift("lr")) shifter_4 (
    .in({out_request[9], out_request[7], out_request[5], out_request[3], out_request[1]}), .\dist (S),
    .out(shifter_4_out));
  Shifter #(.width(5)) shifter_5 (
    .in({out_request[8], out_request[6], out_request[4], out_request[2], out_request[0]}),
    .\dist (subtractor_2_out), .out(shifter_5_out));
  Shifter #(.width(5)) shifter_6 (
    .in({out_request[9], out_request[7], out_request[5], out_request[3], out_request[1]}),
    .\dist (subtractor_3_out), .out(shifter_6_out));
  Shifter #(.width(5)) shifter_7 (
    .in({out_request[8], out_request[6], out_request[4], out_request[2], out_request[0]}),
    .\dist (subtractor_4_out), .out(shifter_7_out));
  Shifter #(.width(5)) shifter_8 (
    .in({out_request[9], out_request[7], out_request[5], out_request[3], out_request[1]}),
    .\dist (subtractor_5_out), .out(shifter_8_out));
  Comparator #(.width(5), .mode("unsigned")) comparator_1 (
    .a(shifter_1_out), .b({5{1'b0}}), .gt(comparator_1_gt));  // open: eq, lt
  Comparator #(.width(5)) comparator_2 (.a(shifter_2_out), .b({5{1'b0}}), .gt(comparator_2_gt));  // open: eq, lt
  Comparator #(.width(5), .mode("unsigned")) comparator_3 (
    .a(shifter_3_out), .b({5{1'b0}}), .gt(comparator_3_gt));  // open: eq, lt
  Comparator #(.width(5), .mode("unsigned")) comparator_4 (
    .a(shifter_4_out), .b({5{1'b0}}), .gt(comparator_4_gt));  // open: eq, lt
  Comparator #(.width(5), .mode("unsigned")) comparator_5 (
    .a(shifter_7_out), .b({5{1'b0}}), .gt(comparator_5_gt));  // open: eq, lt
  Comparator #(.width(5), .mode("unsigned")) comparator_6 (
    .a(shifter_8_out), .b({5{1'b0}}), .gt(comparator_6_gt));  // open: eq, lt
  \_11状态  \u_11状态_1  (
    .in_up(comparator_2_gt), .in_down(comparator_1_gt), .out_up_down(comparator_3_gt),
    .out_up_up(comparator_4_gt), .out_down_down(comparator_5_gt), .out_down_up(comparator_6_gt),
    .next_0(_00_0), .next_1(_00_1));

  // Other names for the same wires on the sheet: out_request_down[4:0] = {out_request[8], out_request[6], out_request[4], out_request[2], out_request[0]};
  //   out_request_up[4:0] = {out_request[9], out_request[7], out_request[5], out_request[3], out_request[1]}

  // Notes on the sheet:
  //   表示楼下有in_quest
  //   表示楼上有in_quest
  //   表示楼上有out_quest_down
  //   表示楼上有out_quest_up
  //   表示楼下有out_quest_down
  //   表示楼下有out_quest_up
endmodule

module \_11状态  (
  input  in_up,
  input  in_down,
  input  out_up_down,
  input  out_up_up,
  input  out_down_down,
  input  out_down_up,
  output next_0,
  output next_1
);

  or or_1 (next_0, in_up, in_down, out_up_down, out_up_up, out_down_up, out_down_down);
  or or_2 (next_1, in_down, out_down_up, out_down_down);
endmodule

module \梯外  (
  input  in_1,
  input  [9:0] in_2,
  input  in_3,
  input  in_4,
  input  in_5,
  input  in_6,
  input  in_7,
  input  in_8,
  input  in_9,
  output [7:0] out_10,
  output [8:0] out_11,
  output [8:0] out_12,
  output [8:0] out_13,
  output [8:0] out_14,
  output [8:0] out_15,
  output [8:0] out_16,
  output [8:0] out_17,
  output [8:0] out_18
);

  Multiplexer #(.width(9), .enable("false")) multiplexer_1 (.in0({9{1'b0}}), .in1(9'h9a), .out(out_15), .sel(in_2[8]));
  Multiplexer #(.width(9), .enable("false")) multiplexer_2 (.in0({9{1'b0}}), .in1(9'h9a), .out(out_16), .sel(in_2[6]));
  Multiplexer #(.width(9), .enable("false")) multiplexer_3 (.in0({9{1'b0}}), .in1(9'h9a), .out(out_17), .sel(in_2[4]));
  Multiplexer #(.width(9), .enable("false")) multiplexer_4 (.in0({9{1'b0}}), .in1(9'h9a), .out(out_18), .sel(in_2[2]));
  Multiplexer #(.width(9), .enable("false")) multiplexer_5 (.in0({9{1'b0}}), .in1(9'hb2), .out(out_11), .sel(in_2[7]));
  Multiplexer #(.width(9), .enable("false")) multiplexer_6 (.in0({9{1'b0}}), .in1(9'hb2), .out(out_12), .sel(in_2[5]));
  Multiplexer #(.width(9), .enable("false")) multiplexer_7 (.in0({9{1'b0}}), .in1(9'hb2), .out(out_13), .sel(in_2[3]));
  Multiplexer #(.width(9), .enable("false")) multiplexer_8 (.in0({9{1'b0}}), .in1(9'hb2), .out(out_14), .sel(in_2[1]));

  assign out_10 = {in_1, in_3, in_4, in_5, in_6, in_7, in_8, in_9};
endmodule

module \梯内  (
  input  in_1,
  input  in_2,
  input  in_3,
  input  in_4,
  input  in_5,
  output [4:0] out_6
);


  assign out_6 = {in_1, in_2, in_3, in_4, in_5};
endmodule

module \楼层  (
  input  [4:0] in_1,
  output out_2,
  output out_3,
  output out_4,
  output out_5,
  output out_6
);


  assign out_2 = in_1[4];
  assign out_3 = in_1[3];
  assign out_4 = in_1[2];
  assign out_5 = in_1[1];
  assign out_6 = in_1[0];
endmodule

module \内部控制面板的上下楼  (
  input  [1:0] up_down,
  output [6:0] out_2,
  output [6:0] out_3,
  output [6:0] out_4,
  output [6:0] out_5,
  output [6:0] out_6
);

  Multiplexer #(.select(2), .width(7), .enable("false")) multiplexer_1 (
    .in0({7{1'b0}}), .in1(7'b0010000), .in3(7'b0000100), .out(out_2), .sel(up_down));  // open: in2
  Multiplexer #(.select(2), .width(7), .enable("false")) multiplexer_2 (
    .in0({7{1'b0}}), .in1(7'b0100000), .in3(7'b0000010), .out(out_3), .sel(up_down));  // open: in2
  Multiplexer #(.select(2), .width(7), .enable("false")) multiplexer_3 (
    .in0({7{1'b0}}), .in1({7{1'b1}}), .in3({7{1'b1}}), .out(out_4), .sel(up_down));  // open: in2
  Multiplexer #(.select(2), .width(7), .enable("false")) multiplexer_4 (
    .in0({7{1'b0}}), .in1(7'b0100000), .in3(7'b0000010), .out(out_5), .sel(up_down));  // open: in2
  Multiplexer #(.select(2), .width(7), .enable("false")) multiplexer_5 (
    .in0({7{1'b0}}), .in1(7'b0010000), .in3(7'b0000100), .out(out_6), .sel(up_down));  // open: in2
endmodule
